# Fritzing sketch CircuitoControlGrua (saved by Fritzing 0.9.3b)
breadboards: 1

parts:
  U1 = RELAY [package=relay-g5q]
  U2 = RELAY [package=relay-g5q]  # not connected
  U3 = RELAY [package=relay-g5q]  # not connected
  U4 = RELAY [package=relay-g5q]  # not connected
  WeMos_D1_Mini1 = WeMos D1 Mini

nets:
  N1: U1.COIL1, WeMos_D1_Mini1.D0
